// Logisim project AR8.circ as structural Verilog: 42 circuits, main circuit ADD1BitComplete
module ADD1BitComplete (
  input  c,
  input  a,
  input  b,
  output s,
  output r
);

  wire add1bit_1_r, add1bit_1_s, add1bit_2_r;

  ADD1Bit add1bit_1 (.a(a), .b(b), .s(add1bit_1_s), .r(add1bit_1_r));
  ADD1Bit add1bit_2 (.a(add1bit_1_s), .b(c), .s(s), .r(add1bit_2_r));
  or or_1 (r, add1bit_2_r, add1bit_1_r);

  // Notes on the sheet:
  //   a: initial=0x1
endmodule

module ADD1Bit (
  input  a,
  input  b,
  output s,
  output r
);

  xor xor_1 (s, a, b);
  and and_1 (r, a, b);

  // Notes on the sheet:
  //   a: initial=0x1
endmodule

module ADD8Bits (
  input  [7:0] A,
  input  [7:0] B,
  output [7:0] S,
  output O
);

  wire add1bit_1_r, add1bitcomplete_1_r, add1bitcomplete_2_r, add1bitcomplete_3_r, add1bitcomplete_4_r,
       add1bitcomplete_5_r, add1bitcomplete_6_r;

  ADD1Bit add1bit_1 (.a(A[0]), .b(B[0]), .s(S[0]), .r(add1bit_1_r));
  ADD1BitComplete add1bitcomplete_1 (.c(add1bit_1_r), .a(A[1]), .b(B[1]), .s(S[1]), .r(add1bitcomplete_1_r));
  ADD1BitComplete add1bitcomplete_2 (.c(add1bitcomplete_1_r), .a(A[2]), .b(B[2]), .s(S[2]), .r(add1bitcomplete_2_r));
  ADD1BitComplete add1bitcomplete_3 (.c(add1bitcomplete_2_r), .a(A[3]), .b(B[3]), .s(S[3]), .r(add1bitcomplete_3_r));
  ADD1BitComplete add1bitcomplete_4 (.c(add1bitcomplete_3_r), .a(A[4]), .b(B[4]), .s(S[4]), .r(add1bitcomplete_4_r));
  ADD1BitComplete add1bitcomplete_5 (.c(add1bitcomplete_4_r), .a(A[5]), .b(B[5]), .s(S[5]), .r(add1bitcomplete_5_r));
  ADD1BitComplete add1bitcomplete_6 (.c(add1bitcomplete_5_r), .a(A[6]), .b(B[6]), .s(S[6]), .r(add1bitcomplete_6_r));
  ADD1BitComplete add1bitcomplete_7 (.c(add1bitcomplete_6_r), .a(A[7]), .b(B[7]), .s(S[7]), .r(O));
endmodule

module NOT8Bits (
  input  [7:0] A,
  output [7:0] S
);

  assign S = ~A;  // NOT_Gate not_1, 8 bits wide
endmodule

module COMPLEMENT8BIts (
  input  [7:0] A,
  output [7:0] S
);

  wire [7:0] not8bits_1_s;

  NOT8Bits not8bits_1 (.A(A), .S(not8bits_1_s));
  ADD8Bits add8bits_1 (.A(not8bits_1_s), .B(8'h1), .S(S));  // open: O
endmodule

module SUB8Bits (
  input  [7:0] A,
  input  [7:0] B,
  output [7:0] S
);

  wire [7:0] complement8bits_1_s;

  COMPLEMENT8BIts complement8bits_1 (.A(B), .S(complement8bits_1_s));
  ADD8Bits add8bits_1 (.A(A), .B(complement8bits_1_s), .S(S));  // open: O
endmodule

module ArithmeticBlock (
  input  [7:0] A,
  input  [7:0] B,
  input  [2:0] OP,
  output [7:0] S,
  output E
);

  wire add8bits_1_o;
  wire [7:0] add8bits_1_s, sub8bits_1_s;

  ADD8Bits add8bits_1 (.A(A), .B(B), .S(add8bits_1_s), .O(add8bits_1_o));
  SUB8Bits sub8bits_1 (.A(A), .B(B), .S(sub8bits_1_s));
  Multiplexer #(.width(8)) multiplexer_1 (.in0(add8bits_1_s), .in1(sub8bits_1_s), .out(S), .sel(OP[0]));
  Multiplexer multiplexer_2 (.in0(add8bits_1_o), .in1(1'b0), .out(E), .sel(OP[0]));
endmodule

module COMPARATOR1Bit (
  input  a,
  input  b,
  output i,
  output e,
  output s
);

  wire not_1_out, not_2_out, xor_1_out;

  not not_1 (not_1_out, a);
  xor xor_1 (xor_1_out, a, b);
  not not_2 (not_2_out, b);
  and and_1 (i, not_1_out, b);
  not not_3 (e, xor_1_out);
  and and_2 (s, a, not_2_out);

  // Notes on the sheet:
  //   a: initial=0x1
endmodule

module COMPARATOR1BitComplete (
  input  iin,
  input  ein,
  input  sin,
  input  a,
  input  b,
  output i,
  output e,
  output s
);

  wire and_1_out, and_2_out, comparator1bit_1_e, comparator1bit_1_i, comparator1bit_1_s;

  COMPARATOR1Bit comparator1bit_1 (
    .a(a), .b(b), .i(comparator1bit_1_i), .e(comparator1bit_1_e), .s(comparator1bit_1_s));
  and and_1 (and_1_out, comparator1bit_1_i, ein);
  and and_2 (and_2_out, comparator1bit_1_s, ein);
  or or_1 (i, iin, and_1_out);
  and and_3 (e, comparator1bit_1_e, ein);
  or or_2 (s, and_2_out, sin);

  // Notes on the sheet:
  //   a: initial=0x1
  //   iin: initial=0x1
endmodule

module COMPARATOR8Bits (
  input  [7:0] A,
  input  [7:0] B,
  output i,
  output e,
  output s
);

  wire comparator1bit_1_e, comparator1bit_1_i, comparator1bit_1_s, comparator1bitcomplete_2_e,
       comparator1bitcomplete_2_i, comparator1bitcomplete_2_s, comparator1bitcomplete_3_e,
       comparator1bitcomplete_3_i, comparator1bitcomplete_3_s, comparator1bitcomplete_4_e,
       comparator1bitcomplete_4_i, comparator1bitcomplete_4_s, comparator1bitcomplete_5_e,
       comparator1bitcomplete_5_i, comparator1bitcomplete_5_s, comparator1bitcomplete_6_e,
       comparator1bitcomplete_6_i, comparator1bitcomplete_6_s, comparator1bitcomplete_7_e,
       comparator1bitcomplete_7_i, comparator1bitcomplete_7_s;

  COMPARATOR1BitComplete comparator1bitcomplete_1 (
    .iin(comparator1bitcomplete_2_i), .ein(comparator1bitcomplete_2_e), .sin(comparator1bitcomplete_2_s),
    .a(A[0]), .b(B[0]), .i(i), .e(e), .s(s));
  COMPARATOR1BitComplete comparator1bitcomplete_2 (
    .iin(comparator1bitcomplete_3_i), .ein(comparator1bitcomplete_3_e), .sin(comparator1bitcomplete_3_s),
    .a(A[1]), .b(B[1]), .i(comparator1bitcomplete_2_i), .e(comparator1bitcomplete_2_e),
    .s(comparator1bitcomplete_2_s));
  COMPARATOR1BitComplete comparator1bitcomplete_3 (
    .iin(comparator1bitcomplete_4_i), .ein(comparator1bitcomplete_4_e), .sin(comparator1bitcomplete_4_s),
    .a(A[2]), .b(B[2]), .i(comparator1bitcomplete_3_i), .e(comparator1bitcomplete_3_e),
    .s(comparator1bitcomplete_3_s));
  COMPARATOR1BitComplete comparator1bitcomplete_4 (
    .iin(comparator1bitcomplete_5_i), .ein(comparator1bitcomplete_5_e), .sin(comparator1bitcomplete_5_s),
    .a(A[3]), .b(B[3]), .i(comparator1bitcomplete_4_i), .e(comparator1bitcomplete_4_e),
    .s(comparator1bitcomplete_4_s));
  COMPARATOR1BitComplete comparator1bitcomplete_5 (
    .iin(comparator1bitcomplete_6_i), .ein(comparator1bitcomplete_6_e), .sin(comparator1bitcomplete_6_s),
    .a(A[4]), .b(B[4]), .i(comparator1bitcomplete_5_i), .e(comparator1bitcomplete_5_e),
    .s(comparator1bitcomplete_5_s));
  COMPARATOR1BitComplete comparator1bitcomplete_6 (
    .iin(comparator1bitcomplete_7_i), .ein(comparator1bitcomplete_7_e), .sin(comparator1bitcomplete_7_s),
    .a(A[5]), .b(B[5]), .i(comparator1bitcomplete_6_i), .e(comparator1bitcomplete_6_e),
    .s(comparator1bitcomplete_6_s));
  COMPARATOR1BitComplete comparator1bitcomplete_7 (
    .iin(comparator1bit_1_i), .ein(comparator1bit_1_e), .sin(comparator1bit_1_s), .a(A[6]), .b(B[6]),
    .i(comparator1bitcomplete_7_i), .e(comparator1bitcomplete_7_e), .s(comparator1bitcomplete_7_s));
  COMPARATOR1Bit comparator1bit_1 (
    .a(A[7]), .b(B[7]), .i(comparator1bit_1_i), .e(comparator1bit_1_e), .s(comparator1bit_1_s));
endmodule

module EQUAL8Bits (
  input  [7:0] A,
  input  [7:0] B,
  output e
);

  COMPARATOR8Bits comparator8bits_1 (.A(A), .B(B), .e(e));  // open: i, s
endmodule

module DIFF8Bits (
  input  [7:0] A,
  input  [7:0] B,
  output d
);

  wire equal8bits_1_e;

  EQUAL8Bits equal8bits_1 (.A(A), .B(B), .e(equal8bits_1_e));
  not not_1 (d, equal8bits_1_e);
endmodule

module SUP8Bits (
  input  [7:0] A,
  input  [7:0] B,
  output s
);

  COMPARATOR8Bits comparator8bits_1 (.A(A), .B(B), .s(s));  // open: i, e
endmodule

module INF8Bits (
  input  [7:0] A,
  input  [7:0] B,
  output i
);

  COMPARATOR8Bits comparator8bits_1 (.A(A), .B(B), .i(i));  // open: e, s
endmodule

module LSL8Bits (
  input  [7:0] A,
  input  [2:0] D,
  output [7:0] S
);

  Multiplexer #(.select(3)) multiplexer_1 (
    .in0(A[0]), .in1(1'b0), .in2(1'b0), .in3(1'b0), .in4(1'b0), .in5(1'b0), .in6(1'b0), .in7(1'b0),
    .out(S[0]), .sel(D));
  Multiplexer #(.select(3)) multiplexer_2 (
    .in0(A[1]), .in1(A[0]), .in2(1'b0), .in3(1'b0), .in4(1'b0), .in5(1'b0), .in6(1'b0), .in7(1'b0),
    .out(S[1]), .sel(D));
  Multiplexer #(.select(3)) multiplexer_3 (
    .in0(A[2]), .in1(A[1]), .in2(A[0]), .in3(1'b0), .in4(1'b0), .in5(1'b0), .in6(1'b0), .in7(1'b0),
    .out(S[2]), .sel(D));
  Multiplexer #(.select(3)) multiplexer_4 (
    .in0(A[3]), .in1(A[2]), .in2(A[1]), .in3(A[0]), .in4(1'b0), .in5(1'b0), .in6(1'b0), .in7(1'b0),
    .out(S[3]), .sel(D));
  Multiplexer #(.select(3)) multiplexer_5 (
    .in0(A[4]), .in1(A[3]), .in2(A[2]), .in3(A[1]), .in4(A[0]), .in5(1'b0), .in6(1'b0), .in7(1'b0),
    .out(S[4]), .sel(D));
  Multiplexer #(.select(3)) multiplexer_6 (
    .in0(A[5]), .in1(A[4]), .in2(A[3]), .in3(A[2]), .in4(A[1]), .in5(A[0]), .in6(1'b0), .in7(1'b0),
    .out(S[5]), .sel(D));
  Multiplexer #(.select(3)) multiplexer_7 (
    .in0(A[6]), .in1(A[5]), .in2(A[4]), .in3(A[3]), .in4(A[2]), .in5(A[1]), .in6(A[0]), .in7(1'b0),
    .out(S[6]), .sel(D));
  Multiplexer #(.select(3)) multiplexer_8 (
    .in0(A[7]), .in1(A[6]), .in2(A[5]), .in3(A[4]), .in4(A[3]), .in5(A[2]), .in6(A[1]), .in7(A[0]),
    .out(S[7]), .sel(D));
endmodule

module LSR8Bits (
  input  [7:0] A,
  input  [2:0] D,
  output [7:0] S
);

  wire [7:0] inverter8bits_1_s, lsl8bits_1_s;

  INVERTER8Bits inverter8bits_1 (.A(A), .S(inverter8bits_1_s));
  LSL8Bits lsl8bits_1 (.A(inverter8bits_1_s), .D(D), .S(lsl8bits_1_s));
  INVERTER8Bits inverter8bits_2 (.A(lsl8bits_1_s), .S(S));
endmodule

module INVERTER8Bits (
  input  [7:0] A,
  output [7:0] S
);


  assign S = {A[0], A[1], A[2], A[3], A[4], A[5], A[6], A[7]};
endmodule

module ROL8Bits (
  input  [7:0] A,
  input  [2:0] D,
  output [7:0] S
);

  Multiplexer #(.select(3)) multiplexer_1 (
    .in0(A[0]), .in1(A[7]), .in2(A[6]), .in3(A[5]), .in4(A[4]), .in5(A[3]), .in6(A[2]), .in7(A[1]),
    .out(S[0]), .sel(D));
  Multiplexer #(.select(3)) multiplexer_2 (
    .in0(A[1]), .in1(A[0]), .in2(A[7]), .in3(A[6]), .in4(A[5]), .in5(A[4]), .in6(A[3]), .in7(A[2]),
    .out(S[1]), .sel(D));
  Multiplexer #(.select(3)) multiplexer_3 (
    .in0(A[2]), .in1(A[1]), .in2(A[0]), .in3(A[7]), .in4(A[6]), .in5(A[5]), .in6(A[4]), .in7(A[3]),
    .out(S[2]), .sel(D));
  Multiplexer #(.select(3)) multiplexer_4 (
    .in0(A[3]), .in1(A[2]), .in2(A[1]), .in3(A[0]), .in4(A[7]), .in5(A[6]), .in6(A[5]), .in7(A[4]),
    .out(S[3]), .sel(D));
  Multiplexer #(.select(3)) multiplexer_5 (
    .in0(A[4]), .in1(A[3]), .in2(A[2]), .in3(A[1]), .in4(A[0]), .in5(A[7]), .in6(A[6]), .in7(A[5]),
    .out(S[4]), .sel(D));
  Multiplexer #(.select(3)) multiplexer_6 (
    .in0(A[5]), .in1(A[4]), .in2(A[3]), .in3(A[2]), .in4(A[1]), .in5(A[0]), .in6(A[7]), .in7(A[6]),
    .out(S[5]), .sel(D));
  Multiplexer #(.select(3)) multiplexer_7 (
    .in0(A[6]), .in1(A[5]), .in2(A[4]), .in3(A[3]), .in4(A[2]), .in5(A[1]), .in6(A[0]), .in7(A[7]),
    .out(S[6]), .sel(D));
  Multiplexer #(.select(3)) multiplexer_8 (
    .in0(A[7]), .in1(A[6]), .in2(A[5]), .in3(A[4]), .in4(A[3]), .in5(A[2]), .in6(A[1]), .in7(A[0]),
    .out(S[7]), .sel(D));
endmodule

module ROR8Bits (
  input  [7:0] A,
  input  [2:0] D,
  output [7:0] S
);

  wire [2:0] not_1_out;
  wire [7:0] rol8bits_1_s;

  assign not_1_out = ~D;  // NOT_Gate not_1, 3 bits wide
  ROL8Bits rol8bits_1 (.A(A), .D(not_1_out), .S(rol8bits_1_s));
  ROL8Bits rol8bits_2 (.A(rol8bits_1_s), .D(3'b001), .S(S));
endmodule

module ComparisonBlock (
  input  [7:0] A,
  input  [7:0] B,
  input  [2:0] OP,
  output S
);

  wire diff8bits_1_d, equal8bits_1_e, inf8bits_1_i, sup8bits_1_s;

  INF8Bits inf8bits_1 (.A(A), .B(B), .i(inf8bits_1_i));
  EQUAL8Bits equal8bits_1 (.A(A), .B(B), .e(equal8bits_1_e));
  SUP8Bits sup8bits_1 (.A(A), .B(B), .s(sup8bits_1_s));
  DIFF8Bits diff8bits_1 (.A(A), .B(B), .d(diff8bits_1_d));
  Multiplexer #(.select(2)) multiplexer_1 (
    .in0(inf8bits_1_i), .in1(equal8bits_1_e), .in2(sup8bits_1_s), .in3(diff8bits_1_d), .out(S), .sel(OP[1:0]));
endmodule

module AND8Bits (
  input  [7:0] A,
  input  [7:0] B,
  output [7:0] S
);

  assign S = A & B;  // AND_Gate and_1, 8 bits wide
endmodule

module OR8Bits (
  input  [7:0] A,
  input  [7:0] B,
  output [7:0] S
);

  assign S = A | B;  // OR_Gate or_1, 8 bits wide
endmodule

module XOR8Bits (
  input  [7:0] A,
  input  [7:0] B,
  output [7:0] S
);

  assign S = A ^ B;  // XOR_Gate xor_1, 8 bits wide
endmodule

module LogicalBlock (
  input  [7:0] A,
  input  [7:0] B,
  input  [2:0] OP,
  output [7:0] S,
  output E
);

  wire [7:0] and8bits_1_s, or8bits_1_s, xor8bits_1_s;

  AND8Bits and8bits_1 (.A(A), .B(B), .S(and8bits_1_s));
  OR8Bits or8bits_1 (.A(A), .B(B), .S(or8bits_1_s));
  XOR8Bits xor8bits_1 (.A(A), .B(B), .S(xor8bits_1_s));
  Multiplexer #(.select(2), .width(8)) multiplexer_1 (
    .in0(and8bits_1_s), .in1(or8bits_1_s), .in2(xor8bits_1_s), .out(S), .sel(OP[1:0]));  // open: in3
  Multiplexer #(.select(2)) multiplexer_2 (.in0(1'b0), .in1(1'b0), .in2(1'b0), .in3(1'b1), .out(E), .sel(OP[1:0]));
endmodule

module ALU (
  input  [7:0] A,
  input  [7:0] B,
  input  [5:0] OP,
  output [7:0] S,
  output E
);

  wire arithmeticblock_1_e, logicalblock_1_e, offsetandrotationblock_1_e;
  wire [0:0] comparisonblock_1_s;
  wire [7:0] arithmeticblock_1_s, logicalblock_1_s, offsetandrotationblock_1_s;

  ArithmeticBlock arithmeticblock_1 (.A(A), .B(B), .OP(OP[2:0]), .S(arithmeticblock_1_s), .E(arithmeticblock_1_e));
  LogicalBlock logicalblock_1 (.A(A), .B(B), .OP(OP[2:0]), .S(logicalblock_1_s), .E(logicalblock_1_e));
  OffsetAndRotationBlock offsetandrotationblock_1 (
    .A(A), .OP(OP[2:0]), .S(offsetandrotationblock_1_s), .E(offsetandrotationblock_1_e));
  ComparisonBlock comparisonblock_1 (.A(A), .B(B), .OP(OP[2:0]), .S(comparisonblock_1_s[0]));
  Multiplexer #(.select(3), .width(8)) multiplexer_1 (
    .in0(arithmeticblock_1_s), .in1(logicalblock_1_s), .in2(offsetandrotationblock_1_s),
    .in3({{7{1'b0}}, comparisonblock_1_s[0]}), .out(S), .sel(OP[5:3]));  // open: in4, in5, in6, in7
  Multiplexer #(.select(3)) multiplexer_2 (
    .in0(arithmeticblock_1_e), .in1(logicalblock_1_e), .in2(offsetandrotationblock_1_e), .in3(1'b0),
    .in4(1'b1), .in5(1'b1), .in6(1'b1), .in7(1'b1), .out(E), .sel(OP[5:3]));
endmodule

module OffsetAndRotationBlock (
  input  [7:0] A,
  input  [2:0] OP,
  output [7:0] S,
  output E
);

  wire [7:0] asr1_1_s, lsl1_1_s, lsr1_1_s, not8bits_1_s, rol1_1_s, ror1_1_s;

  NOT8Bits not8bits_1 (.A(A), .S(not8bits_1_s));
  LSL1 lsl1_1 (.A(A), .S(lsl1_1_s));
  LSR1 lsr1_1 (.A(A), .S(lsr1_1_s));
  ASR1 asr1_1 (.A(A), .S(asr1_1_s));
  ROL1 rol1_1 (.A(A), .S(rol1_1_s));
  ROR1 ror1_1 (.A(A), .S(ror1_1_s));
  Multiplexer #(.select(3), .width(8)) multiplexer_1 (
    .in0(not8bits_1_s), .in1(lsl1_1_s), .in2(lsr1_1_s), .in3(asr1_1_s), .in4(rol1_1_s), .in5(ror1_1_s),
    .out(S), .sel(OP));  // open: in6, in7
  Multiplexer #(.select(3)) multiplexer_2 (
    .in0(1'b0), .in1(1'b0), .in2(1'b0), .in3(1'b0), .in4(1'b0), .in5(1'b0), .in6(1'b1), .in7(1'b1), .out(E),
    .sel(OP));
endmodule

module LSL1 (
  input  [7:0] A,
  output [7:0] S
);

  LSL8Bits lsl8bits_1 (.A(A), .D(3'b001), .S(S));
endmodule

module LSR1 (
  input  [7:0] A,
  output [7:0] S
);

  LSR8Bits lsr8bits_1 (.A(A), .D(3'b001), .S(S));
endmodule

module ROL1 (
  input  [7:0] A,
  output [7:0] S
);

  ROL8Bits rol8bits_1 (.A(A), .D(3'b001), .S(S));
endmodule

module ROR1 (
  input  [7:0] A,
  output [7:0] S
);

  ROR8Bits ror8bits_1 (.A(A), .D(3'b001), .S(S));
endmodule

module ASR1 (
  input  [7:0] A,
  output [7:0] S
);


  assign S = {{2{A[7]}}, A[6:1]};
endmodule

module REGISTER1Bit (
  input  C,
  input  WE,
  input  CLK,
  output S
);

  wire multiplexer_1_out;

  D_Flip_Flop d_ff_1 (.D(multiplexer_1_out), .clk(CLK), .Q(S));  // open: Qn, preset, reset
  Multiplexer multiplexer_1 (.in0(S), .in1(C), .out(multiplexer_1_out), .sel(WE));
endmodule

module REGISTER8Bits (
  input  [7:0] C,
  input  WE,
  input  CLK,
  output [7:0] S
);

  wire multiplexer_1_out, multiplexer_2_out, multiplexer_3_out, multiplexer_4_out, multiplexer_5_out,
       multiplexer_6_out, multiplexer_7_out, multiplexer_8_out;

  D_Flip_Flop d_ff_1 (.D(multiplexer_1_out), .clk(CLK), .Q(S[0]));  // open: Qn, preset, reset
  Multiplexer multiplexer_1 (.in0(S[0]), .in1(C[0]), .out(multiplexer_1_out), .sel(WE));
  D_Flip_Flop d_ff_2 (.D(multiplexer_2_out), .clk(CLK), .Q(S[1]));  // open: Qn, preset, reset
  Multiplexer multiplexer_2 (.in0(S[1]), .in1(C[1]), .out(multiplexer_2_out), .sel(WE));
  D_Flip_Flop d_ff_3 (.D(multiplexer_3_out), .clk(CLK), .Q(S[2]));  // open: Qn, preset, reset
  Multiplexer multiplexer_3 (.in0(S[2]), .in1(C[2]), .out(multiplexer_3_out), .sel(WE));
  D_Flip_Flop d_ff_4 (.D(multiplexer_4_out), .clk(CLK), .Q(S[3]));  // open: Qn, preset, reset
  Multiplexer multiplexer_4 (.in0(S[3]), .in1(C[3]), .out(multiplexer_4_out), .sel(WE));
  D_Flip_Flop d_ff_5 (.D(multiplexer_5_out), .clk(CLK), .Q(S[4]));  // open: Qn, preset, reset
  Multiplexer multiplexer_5 (.in0(S[4]), .in1(C[4]), .out(multiplexer_5_out), .sel(WE));
  D_Flip_Flop d_ff_6 (.D(multiplexer_6_out), .clk(CLK), .Q(S[5]));  // open: Qn, preset, reset
  Multiplexer multiplexer_6 (.in0(S[5]), .in1(C[5]), .out(multiplexer_6_out), .sel(WE));
  D_Flip_Flop d_ff_7 (.D(multiplexer_7_out), .clk(CLK), .Q(S[6]));  // open: Qn, preset, reset
  Multiplexer multiplexer_7 (.in0(S[6]), .in1(C[6]), .out(multiplexer_7_out), .sel(WE));
  D_Flip_Flop d_ff_8 (.D(multiplexer_8_out), .clk(CLK), .Q(S[7]));  // open: Qn, preset, reset
  Multiplexer multiplexer_8 (.in0(S[7]), .in1(C[7]), .out(multiplexer_8_out), .sel(WE));
endmodule

module DECODE (
  input  [23:0] I,
  input  WE,
  output RFWE,
  output [2:0] slctC,
  output [2:0] slctB,
  output [2:0] slctA,
  output [5:0] slctOP
);

  wire and_1_out, and_2_out, and_3_out, and_4_out, and_6_out, and_7_out, CLK_out, not_2_out, not_4_out,
       not_5_out, not_6_out, not_7_out, or_2_out;
  wire [2:0] register24bits_1_s_2, register24bits_1_s_3;
  wire [23:3] register24bits_1_s;

  Clock CLK (.out(CLK_out));
  REGISTER24Bits register24bits_1 (
    .C(I), .WE(WE), .CLK(CLK_out),
    .S({register24bits_1_s[23:15], slctA, register24bits_1_s[11], register24bits_1_s_2, register24bits_1_s[7:3], register24bits_1_s_3}));
  or or_1 (RFWE, register24bits_1_s_3[0], register24bits_1_s_3[1], register24bits_1_s_3[2], register24bits_1_s[3], register24bits_1_s[4], register24bits_1_s[5], register24bits_1_s[6], register24bits_1_s[7], register24bits_1_s_2[0], register24bits_1_s_2[1], register24bits_1_s_2[2], register24bits_1_s[11], slctA[0], slctA[1], slctA[2], register24bits_1_s[15], register24bits_1_s[16], register24bits_1_s[17], register24bits_1_s[18], register24bits_1_s[19], register24bits_1_s[20], register24bits_1_s[21], register24bits_1_s[22], register24bits_1_s[23]);
  or or_2 (or_2_out, register24bits_1_s[19], register24bits_1_s[20]);
  not not_1 (slctOP[4], register24bits_1_s[20]);
  not not_2 (not_2_out, or_2_out);
  not not_3 (slctOP[3], register24bits_1_s[19]);
  and and_1 (and_1_out, or_2_out, register24bits_1_s[17]);
  and and_2 (and_2_out, not_2_out, register24bits_1_s[18]);
  and and_3 (and_3_out, or_2_out, register24bits_1_s[16]);
  and and_4 (and_4_out, not_2_out, register24bits_1_s[17]);
  not not_4 (not_4_out, register24bits_1_s[20]);
  and and_5 (slctOP[2], register24bits_1_s[18], or_2_out);
  or or_3 (slctOP[1], and_1_out, and_2_out);
  or or_4 (slctOP[0], and_3_out, and_4_out);
  Multiplexer #(.width(3)) multiplexer_1 (.in0(3'b000), .in1(register24bits_1_s_2), .out(slctB), .sel(not_5_out));
  not not_5 (not_5_out, and_6_out);
  and and_6 (and_6_out, not_4_out, register24bits_1_s[19]);
  Multiplexer #(.width(3)) multiplexer_2 (.in0(3'b111), .in1(register24bits_1_s_3), .out(slctC), .sel(not_6_out));
  not not_6 (not_6_out, and_7_out);
  and and_7 (and_7_out, not_4_out, not_7_out);
  not not_7 (not_7_out, register24bits_1_s[19]);

  assign slctOP[5] = 1'b0;
endmodule

module REGISTERFILE (
  input  [7:0] C,
  input  WE1,
  input  WE2,
  input  WE3,
  input  WE4,
  input  WE5,
  input  WE6,
  input  WE7,
  input  WE8,
  output [7:0] R1,
  output [7:0] R2,
  output [7:0] R3,
  output [7:0] R4,
  output [7:0] R5,
  output [7:0] R6,
  output [7:0] R7,
  output RCMP
);

  wire CLK_out;

  Clock CLK (.out(CLK_out));
  REGISTER8Bits register8bits_1 (.C(C), .WE(WE1), .CLK(CLK_out), .S(R1));
  REGISTER8Bits register8bits_2 (.C(C), .WE(WE2), .CLK(CLK_out), .S(R2));
  REGISTER8Bits register8bits_3 (.C(C), .WE(WE3), .CLK(CLK_out), .S(R3));
  REGISTER8Bits register8bits_4 (.C(C), .WE(WE4), .CLK(CLK_out), .S(R4));
  REGISTER8Bits register8bits_5 (.C(C), .WE(WE5), .CLK(CLK_out), .S(R5));
  REGISTER8Bits register8bits_6 (.C(C), .WE(WE6), .CLK(CLK_out), .S(R6));
  REGISTER8Bits register8bits_7 (.C(C), .WE(WE7), .CLK(CLK_out), .S(R7));
  REGISTER1Bit register1bit_1 (.C(C[0]), .WE(WE8), .CLK(CLK_out), .S(RCMP));
endmodule

module AR8PROCESSORTEST (
);

  wire clock_1_out, decode_1_rfwe, decoder_1_out0, decoder_1_out1, decoder_1_out2, decoder_1_out3,
       decoder_1_out4, decoder_1_out5, decoder_1_out6, decoder_1_out7;
  wire [0:0] registerfile_1_rcmp;
  wire [2:0] decode_1_slcta, decode_1_slctb, decode_1_slctc;
  wire [5:0] decode_1_slctop;
  wire [7:0] alu_1_s, inc8bits_1_s, multiplexer_1_out, multiplexer_2_out, pc_1_s, registerfile_1_r1,
       registerfile_1_r2, registerfile_1_r3, registerfile_1_r4, registerfile_1_r5, registerfile_1_r6,
       registerfile_1_r7;
  wire [23:0] fetch_1_s, ram_1_dout;

  RAM #(.dataWidth(24)) ram_1 (.addr(pc_1_s), .we(1'b0), .oe(1'b1), .clk(clock_1_out), .dout(ram_1_dout));  // open: din
  Clock clock_1 (.out(clock_1_out));
  PC pc_1 (.C(inc8bits_1_s), .WE(1'b1), .S(pc_1_s));
  INC8Bits inc8bits_1 (.A(pc_1_s), .S(inc8bits_1_s));
  FETCH fetch_1 (.C(ram_1_dout), .WE(1'b1), .S(fetch_1_s));
  Decoder #(.select(3)) decoder_1 (
    .out0(decoder_1_out0), .out1(decoder_1_out1), .out2(decoder_1_out2), .out3(decoder_1_out3),
    .out4(decoder_1_out4), .out5(decoder_1_out5), .out6(decoder_1_out6), .out7(decoder_1_out7),
    .sel(decode_1_slctc), .en(decode_1_rfwe));
  DECODE decode_1 (
    .I(fetch_1_s), .WE(1'b1), .slctA(decode_1_slcta), .slctOP(decode_1_slctop), .slctB(decode_1_slctb),
    .slctC(decode_1_slctc), .RFWE(decode_1_rfwe));
  REGISTERFILE registerfile_1 (
    .WE1(decoder_1_out0), .WE2(decoder_1_out1), .WE3(decoder_1_out2), .WE4(decoder_1_out3),
    .WE5(decoder_1_out4), .WE6(decoder_1_out5), .WE7(decoder_1_out6), .WE8(decoder_1_out7), .C(alu_1_s),
    .R1(registerfile_1_r1), .R2(registerfile_1_r2), .R3(registerfile_1_r3), .R4(registerfile_1_r4),
    .R5(registerfile_1_r5), .R6(registerfile_1_r6), .R7(registerfile_1_r7), .RCMP(registerfile_1_rcmp[0]));
  Multiplexer #(.select(3), .width(8)) multiplexer_1 (
    .in0(registerfile_1_r1), .in1(registerfile_1_r2), .in2(registerfile_1_r3), .in3(registerfile_1_r4),
    .in4(registerfile_1_r5), .in5(registerfile_1_r6), .in6(registerfile_1_r7),
    .in7({{7{1'b0}}, registerfile_1_rcmp[0]}), .out(multiplexer_1_out), .sel(decode_1_slctb));
  Multiplexer #(.select(3), .width(8)) multiplexer_2 (
    .in0(registerfile_1_r1), .in1(registerfile_1_r2), .in2(registerfile_1_r3), .in3(registerfile_1_r4),
    .in4(registerfile_1_r5), .in5(registerfile_1_r6), .in6(registerfile_1_r7),
    .in7({{7{1'b0}}, registerfile_1_rcmp[0]}), .out(multiplexer_2_out), .sel(decode_1_slcta));
  ALU alu_1 (.A(multiplexer_2_out), .OP(decode_1_slctop), .B(multiplexer_1_out), .S(alu_1_s));  // open: E
endmodule

module REGISTER24Bits (
  input  [23:0] C,
  input  WE,
  input  CLK,
  output [23:0] S
);

  REGISTER8Bits register8bits_1 (.C(C[7:0]), .WE(WE), .CLK(CLK), .S(S[7:0]));
  REGISTER8Bits register8bits_2 (.C(C[15:8]), .WE(WE), .CLK(CLK), .S(S[15:8]));
  REGISTER8Bits register8bits_3 (.C(C[23:16]), .WE(WE), .CLK(CLK), .S(S[23:16]));
endmodule

module FETCH (
  input  [23:0] C,
  input  WE,
  output [23:0] S
);

  wire CLK_out;

  Clock CLK (.out(CLK_out));
  REGISTER24Bits register24bits_1 (.C(C), .WE(WE), .CLK(CLK_out), .S(S));
endmodule

module PC (
  input  [7:0] C,
  input  WE,
  output [7:0] S
);

  wire CLK_out;

  Clock CLK (.out(CLK_out));
  REGISTER8Bits register8bits_1 (.C(C), .WE(WE), .CLK(CLK_out), .S(S));
endmodule

module INC8Bits (
  input  [7:0] A,
  output [7:0] S
);

  ADD8Bits add8bits_1 (.A(A), .B(8'h1), .S(S));  // open: O
endmodule

module AR8PROCESSOR (
);

  wire clock_1_out, decode_1_rfwe, decoder_1_out0, decoder_1_out1, decoder_1_out2, decoder_1_out3,
       decoder_1_out4, decoder_1_out5, decoder_1_out6, decoder_1_out7;
  wire [0:0] registerfile_1_rcmp;
  wire [2:0] decode_1_slcta, decode_1_slctb, decode_1_slctc;
  wire [5:0] decode_1_slctop;
  wire [7:0] alu_1_s, inc8bits_1_s, multiplexer_1_out, multiplexer_2_out, pc_1_s, registerfile_1_r1,
       registerfile_1_r2, registerfile_1_r3, registerfile_1_r4, registerfile_1_r5, registerfile_1_r6,
       registerfile_1_r7;
  wire [23:0] fetch_1_s, ram_1_dout;

  PC pc_1 (.C(inc8bits_1_s), .WE(1'b1), .S(pc_1_s));
  Clock clock_1 (.out(clock_1_out));
  RAM #(.dataWidth(24)) ram_1 (.addr(pc_1_s), .we(1'b0), .oe(1'b1), .clk(clock_1_out), .dout(ram_1_dout));  // open: din
  INC8Bits inc8bits_1 (.A(pc_1_s), .S(inc8bits_1_s));
  FETCH fetch_1 (.C(ram_1_dout), .WE(1'b1), .S(fetch_1_s));
  Decoder #(.select(3)) decoder_1 (
    .out0(decoder_1_out0), .out1(decoder_1_out1), .out2(decoder_1_out2), .out3(decoder_1_out3),
    .out4(decoder_1_out4), .out5(decoder_1_out5), .out6(decoder_1_out6), .out7(decoder_1_out7),
    .sel(decode_1_slctc), .en(decode_1_rfwe));
  DECODE decode_1 (
    .I(fetch_1_s), .WE(1'b1), .slctA(decode_1_slcta), .slctOP(decode_1_slctop), .slctB(decode_1_slctb),
    .slctC(decode_1_slctc), .RFWE(decode_1_rfwe));
  REGISTERFILE registerfile_1 (
    .WE1(decoder_1_out0), .WE2(decoder_1_out1), .WE3(decoder_1_out2), .WE4(decoder_1_out3),
    .WE5(decoder_1_out4), .WE6(decoder_1_out5), .WE7(decoder_1_out6), .WE8(decoder_1_out7), .C(alu_1_s),
    .R1(registerfile_1_r1), .R2(registerfile_1_r2), .R3(registerfile_1_r3), .R4(registerfile_1_r4),
    .R5(registerfile_1_r5), .R6(registerfile_1_r6), .R7(registerfile_1_r7), .RCMP(registerfile_1_rcmp[0]));
  Multiplexer #(.select(3), .width(8)) multiplexer_1 (
    .in0(registerfile_1_r1), .in1(registerfile_1_r2), .in2(registerfile_1_r3), .in3(registerfile_1_r4),
    .in4(registerfile_1_r5), .in5(registerfile_1_r6), .in6(registerfile_1_r7),
    .in7({{7{1'b0}}, registerfile_1_rcmp[0]}), .out(multiplexer_1_out), .sel(decode_1_slctb));
  ALU alu_1 (.A(multiplexer_2_out), .OP(decode_1_slctop), .B(multiplexer_1_out), .S(alu_1_s));  // open: E
  Multiplexer #(.select(3), .width(8)) multiplexer_2 (
    .in0(registerfile_1_r1), .in1(registerfile_1_r2), .in2(registerfile_1_r3), .in3(registerfile_1_r4),
    .in4(registerfile_1_r5), .in5(registerfile_1_r6), .in6(registerfile_1_r7),
    .in7({{7{1'b0}}, registerfile_1_rcmp[0]}), .out(multiplexer_2_out), .sel(decode_1_slcta));
endmodule

module test (
);

  AR8PROCESSOR ar8processor_1 ();
  PC pc_1 ();  // open: C, WE, S
  REGISTERFILE registerfile_1 ();  // open: WE1, WE2, WE3, WE4, WE5, WE6, WE7, WE8, C, R1, R2, R3, R4, R5, R6, R7, RCMP
  FETCH fetch_1 ();  // open: C, WE, S
  DECODE decode_1 ();  // open: I, WE, slctA, slctOP, slctB, slctC, RFWE
  ALU alu_1 ();  // open: A, OP, B, S, E
  RAM #(.dataWidth(24)) ram_1 ();  // open: addr, we, oe, clk, din, dout
endmodule
